# Fritzing sketch GPS_Monitor_Teil2 (saved by Fritzing 0.9.3b)
breadboards: 1

parts:
  U1 = NEO 6M GPS
  HD44780_2004_LCD_Display_4x20_characters_Green2 = HD44780 2004 LCD Display 4x20 characters Green
  LCM1602_IIC1 = LCM1602 IIC [part_number="LCM1602 IIC" chip_label="LCM1602 IIC" package="DIP (Dual Inline) [THT]"]
  Nano_V1 = Nano V3
  KY-004_Button_Module1 = KY-004 Button Module

nets:
  N1: U1.RXD, Nano_V1.D3
  N2: U1.TXD, Nano_V1.D4
  GND: U1.GND, LCM1602_IIC1.GND, Nano_V1.GND, KY-004_Button_Module1.-
  VCC: U1.VCC, LCM1602_IIC1.VCC, Nano_V1.5V
  N3: HD44780_2004_LCD_Display_4x20_characters_Green2.VSS, LCM1602_IIC1.K
  N4: HD44780_2004_LCD_Display_4x20_characters_Green2.VDD, LCM1602_IIC1.A
  N5: HD44780_2004_LCD_Display_4x20_characters_Green2.V0, LCM1602_IIC1.D7
  N6: HD44780_2004_LCD_Display_4x20_characters_Green2.RS, LCM1602_IIC1.D6
  N7: HD44780_2004_LCD_Display_4x20_characters_Green2.R/W, LCM1602_IIC1.D5
  N8: HD44780_2004_LCD_Display_4x20_characters_Green2.E, LCM1602_IIC1.D4
  N9: HD44780_2004_LCD_Display_4x20_characters_Green2.DB0, LCM1602_IIC1.D3
  N10: HD44780_2004_LCD_Display_4x20_characters_Green2.DB1, LCM1602_IIC1.D2
  N11: HD44780_2004_LCD_Display_4x20_characters_Green2.DB2, LCM1602_IIC1.D1
  N12: HD44780_2004_LCD_Display_4x20_characters_Green2.DB3, LCM1602_IIC1.D0
  N13: HD44780_2004_LCD_Display_4x20_characters_Green2.DB4, LCM1602_IIC1.E
  N14: HD44780_2004_LCD_Display_4x20_characters_Green2.DB5, LCM1602_IIC1.RW
  N15: HD44780_2004_LCD_Display_4x20_characters_Green2.DB6, LCM1602_IIC1.RS
  N16: HD44780_2004_LCD_Display_4x20_characters_Green2.DB7, LCM1602_IIC1.V0
  N17: HD44780_2004_LCD_Display_4x20_characters_Green2.LED_A, LCM1602_IIC1.VDD
  N18: HD44780_2004_LCD_Display_4x20_characters_Green2.LED_K, LCM1602_IIC1.VSS
  N19: LCM1602_IIC1.SDA, Nano_V1.A4
  N20: LCM1602_IIC1.SCL, Nano_V1.A5
  N21: LCM1602_IIC1.LED_A, LCM1602_IIC1.LED_B
  N22: Nano_V1.D7, KY-004_Button_Module1.Vin

custom parts:
  NEO 6M GPS: uSD module
  HD44780 2004 LCD Display 4x20 characters Green: This 20x4 LCD module with a built-in HD44780 Controller allows for the display of 20x4 characters in black font on a green background. The control of the display, for example, via an Arduino, Raspberry Pi, etc., the connection of The Display can be made directly to the GPIO Ports of the Arduino. The assignment of the 16 contacts looks like the following: VSS: GND (ground VDD: +5V supply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
  LCM1602 IIC: I2C-Module to use a 1602 or 2004 LCD on with the wire.h libory Serial LCD Modul
  Nano V3: Can be used universally thanks to a compact design! By 14 digital in - and outputs and 6 analog inputs on the Nano V3 can also be used for larger projects! Thanks to the ATmega328 micro-controller, as well as more sophisticated programs to be executable! By Arduino compatibility in the Arduino IDE programmable! With FTDI Chip! Usual high quality and fast delivery directly from Germany by order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
  KY-004 Button Module: Universal Button Module for direct use with Arduino, Raspberry & Co. Operating Voltage 3.3 V - 5 V Usual high quality and fast delivery directly from Germany by order AZ Delivery Of course, you will receive when you purchase through AZDelivery fully automatically and guarantees a Invoice incl. VAT and according to German Standards Guaranteed ROHS compliance by purchase from the German trader
