# Fritzing sketch GPS_Monitor_Teil3_Geofence Alarmanlage (saved by Fritzing 0.9.3b)
breadboards: 1

parts:
  U1 = NEO 6M GPS
  Nano_V1 = Nano V3
  KY-004_Button_Module1 = KY-004 Button Module
  LED2 = RGB LED (com. cathode, rgb) [package="5 mm [THT]"]
  R1 = Resistor [tolerance=±5% resistance=100 package="0805 [SMD]"]
  R2 = Resistor [tolerance=±5% resistance=100 package="0805 [SMD]"]
  R3 = Resistor [tolerance=±5% resistance=100 package="0805 [SMD]"]
  U2 = 2-Channel 5v Relay Shield [package=relay-2ch5v10a]

nets:
  N1: U1.RXD, Nano_V1.D3
  N2: U1.TXD, Nano_V1.D4
  GND: U1.GND, Nano_V1.GND, KY-004_Button_Module1.-, LED2.green_anode, U2.GND
  VCC: U1.VCC, Nano_V1.5V, U2.VCC
  N3: Nano_V1.D2, U2.IN1
  N4: Nano_V1.D6, R1.Pin_1
  N5: Nano_V1.D7, R2.Pin_1
  N6: Nano_V1.D8, R3.Pin_1
  N7: Nano_V1.D9, KY-004_Button_Module1.Vin
  N8: LED2.red_anode, R1.Pin_0
  N9: LED2.common_cathode, R2.Pin_0
  N10: LED2.blue_anode, R3.Pin_0

custom parts:
  NEO 6M GPS: uSD module
  Nano V3: Can be used universally thanks to a compact design! By 14 digital in - and outputs and 6 analog inputs on the Nano V3 can also be used for larger projects! Thanks to the ATmega328 micro-controller, as well as more sophisticated programs to be executable! By Arduino compatibility in the Arduino IDE programmable! With FTDI Chip! Usual high quality and fast delivery directly from Germany by order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
  KY-004 Button Module: Universal Button Module for direct use with Arduino, Raspberry & Co. Operating Voltage 3.3 V - 5 V Usual high quality and fast delivery directly from Germany by order AZ Delivery Of course, you will receive when you purchase through AZDelivery fully automatically and guarantees a Invoice incl. VAT and according to German Standards Guaranteed ROHS compliance by purchase from the German trader
  2-Channel 5v Relay Shield: 2 Channel 5v Relay Shield w. 2x SPD-06VDC-SD-C
